# Fritzing sketch in-meeting-indicator (saved by Fritzing 0.9.6b)

parts:
  U1 = NodeMCU V1.0
  LED4 = LED - 5mm [color="Red (633nm)" package="5 mm [THT]"]
  LED5 = LED - 5mm [color="Blue (430nm)" package="5 mm [THT]"]
  Raspberry_Pi_1 = Raspberry Pi 3 [part_number=RPI-3-V1.2]  # not connected

nets:
  N1: U1.GND, LED4.cathode, LED5.cathode
  N2: U1.D5, LED4.anode
  N3: U1.D6, LED5.anode

custom parts:
  NodeMCU V1.0: ESP8266 based NodeMCU
